# Fritzing sketch 01 (saved by Fritzing 0.7.12b)
breadboards: 1

parts:
  LED1 = 8x8 LED Matrix (green)
  Arduino1 = Arduino

nets:
  N1: LED1.+, Arduino1.+5V
  N2: LED1.-, Arduino1.GND
  N3: LED1.D, Arduino1.A4
  N4: LED1.C, Arduino1.A5

custom parts:
  8x8 LED Matrix (green): 8x8 LED Matrix with I2C control (green)
